# Fritzing sketch HC-SR501-PIR (saved by Fritzing 0.9.3b)

parts:
  HC-SR501_PIR = HC-SR501 Body Sensor Module
  Itsy_Bitsy_M0_Express = Itsy Bitsy M0 Express

nets:
  N1: HC-SR501_PIR.VCC, Itsy_Bitsy_M0_Express.D12
  N2: HC-SR501_PIR.OUT, Itsy_Bitsy_M0_Express.VBUS
  GND: HC-SR501_PIR.GND, Itsy_Bitsy_M0_Express.GND

custom parts:
  HC-SR501 Body Sensor Module: Pyroelectric Infrared PIR Motion Sensor Detector Module
  Itsy Bitsy M0 Express: What's smaller than a Feather but larger than a Trinket? It's an Adafruit ItsyBitsy M0 Express! Small, powerful, with a rockin' ATSAMD21 Cortex M0 processor running at 48 MHz - this microcontroller board is perfect when you want something very compact, but still with a bunch of pins. ItsyBitsy M0 Express is only 1.4" long by 0.7" wide, but has 6 power pins, 23 digital GPIO pins (12 of which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
