# Fritzing sketch bark (saved by Fritzing 0.9.3b)

parts:
  Part1 = Mono 2.5W Class D Audio Amplifier - PAM8302
  SP1 = SPEAKER [package=pcb_mount_speaker]
  Part2 = Itsy Bitsy M0 Express
  U2 = POT_SWITCH [package=pot_pth_switch]
  VCC2 = Battery
  HC-SR502 = HC-SR501 Body Sensor Module  # not connected

nets:
  GND: Part1.GND, Part1.AIN-, Part2.GND, U2.G$1_A, VCC2.-
  VCC: Part1.VCC, Part2.+3V3
  N1: Part1.AIN+, U2.G$2_1
  N2: Part1.VO+, SP1.+
  N3: Part1.VO-, SP1.-
  N4: Part2.VBAT, U2.G$1_S
  N5: Part2.A0, U2.G$2_2

custom parts:
  Mono 2.5W Class D Audio Amplifier - PAM8302: A super small but powerful mono amplifier able to deliver up to 2.5 Watts into 4-8 ohm impedance speakers. Inside the miniature chip is a class D controller, able to run from 2.0V-5.5VDC. Since the amp is a class D, its very efficient (over 90% efficient when driving an 8Ω speaker at over half a Watt) - making it perfect for portable and battery-powered projects.
  Itsy Bitsy M0 Express: What's smaller than a Feather but larger than a Trinket? It's an Adafruit ItsyBitsy M0 Express! Small, powerful, with a rockin' ATSAMD21 Cortex M0 processor running at 48 MHz - this microcontroller board is perfect when you want something very compact, but still with a bunch of pins. ItsyBitsy M0 Express is only 1.4" long by 0.7" wide, but has 6 power pins, 23 digital GPIO pins (12 of which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
  HC-SR501 Body Sensor Module: Pyroelectric Infrared PIR Motion Sensor Detector Module
